// Logisim project RGLED.circ as structural Verilog
module \数码管驱动  (
  input  X3,
  input  X2,
  input  X1,
  input  X0,
  output Seg_1,
  output Seg_2,
  output Seg_3,
  output Seg_4,
  output Seg_5,
  output Seg_6,
  output Seg_7
);

  wire and_1_out, and_2_out, and_3_out, and_4_out, and_5_out, and_6_out, and_7_out, and_8_out, and_9_out,
       and_10_out, and_11_out, and_12_out, and_13_out, and_14_out, and_15_out, and_16_out, and_17_out,
       not_1_out, not_2_out, not_3_out, not_4_out, not_5_out, not_6_out, not_7_out, not_8_out, not_9_out,
       not_10_out, not_11_out, not_12_out, not_13_out, not_14_out, not_15_out, not_16_out, not_17_out,
       not_18_out, not_19_out, not_20_out, not_21_out, not_22_out, not_23_out, not_24_out;

  not not_1 (not_1_out, X3);
  not not_2 (not_2_out, X2);
  and and_1 (and_1_out, not_1_out, not_2_out, X1);
  not not_3 (not_3_out, X3);
  and and_2 (and_2_out, not_3_out, X2, not_4_out);
  not not_4 (not_4_out, X0);
  and and_3 (and_3_out, X2, not_5_out);
  not not_5 (not_5_out, X1);
  and and_4 (and_4_out, X3, not_6_out);
  not not_6 (not_6_out, X1);
  not not_7 (not_7_out, X1);
  and and_5 (and_5_out, not_7_out, not_8_out);
  not not_8 (not_8_out, X0);
  and and_6 (and_6_out, X2, not_9_out);
  not not_9 (not_9_out, X1);
  and and_7 (and_7_out, X2, not_10_out);
  not not_10 (not_10_out, X0);
  not not_11 (not_11_out, X2);
  and and_8 (and_8_out, not_11_out, not_12_out);
  not not_12 (not_12_out, X0);
  and and_9 (and_9_out, X2, X0);
  not not_13 (not_13_out, X2);
  not not_14 (not_14_out, X1);
  and and_10 (and_10_out, not_14_out, not_15_out);
  not not_15 (not_15_out, X0);
  and and_11 (and_11_out, X1, X0);
  not not_16 (not_16_out, X2);
  and and_12 (and_12_out, not_16_out, not_17_out);
  not not_17 (not_17_out, X0);
  and and_13 (and_13_out, X1, not_18_out);
  not not_18 (not_18_out, X0);
  not not_19 (not_19_out, X2);
  and and_14 (and_14_out, not_19_out, not_20_out);
  not not_20 (not_20_out, X0);
  not not_21 (not_21_out, X2);
  and and_15 (and_15_out, not_21_out, X1);
  and and_16 (and_16_out, X1, not_22_out);
  not not_22 (not_22_out, X0);
  and and_17 (and_17_out, X2, not_23_out, X0);
  not not_23 (not_23_out, X1);
  not not_24 (not_24_out, X1);
  or or_1 (Seg_1, and_1_out, and_2_out, and_3_out, and_4_out);
  or or_2 (Seg_2, and_5_out, and_6_out, and_7_out, X3);
  or or_3 (Seg_3, and_8_out, X1, and_9_out, X3);
  or or_4 (Seg_4, not_13_out, and_10_out, and_11_out);
  or or_5 (Seg_5, and_12_out, and_13_out);
  or or_6 (Seg_6, and_14_out, and_15_out, and_16_out, and_17_out, X3);
  or or_7 (Seg_7, not_24_out, X0, X2, X3);
endmodule

module \数码管驱动测试  (
);

  wire clock_1_out, \数码管驱动_1_seg_1 , \数码管驱动_1_seg_2 , \数码管驱动_1_seg_3 , \数码管驱动_1_seg_4 , \数码管驱动_1_seg_5 ,
       \数码管驱动_1_seg_6 , \数码管驱动_1_seg_7 ;
  wire [3:0] counter_1_q;

  Counter #(.width(4), .max('hf)) counter_1 (.Q(counter_1_q), .clk(clock_1_out));  // open: load, D, count, carry, clr
  Clock clock_1 (.out(clock_1_out));
  \数码管驱动  \u_数码管驱动_1  (
    .X3(counter_1_q[3]), .X2(counter_1_q[2]), .X1(counter_1_q[1]), .Seg_1(\数码管驱动_1_seg_1 ),
    .X0(counter_1_q[0]), .Seg_2(\数码管驱动_1_seg_2 ), .Seg_3(\数码管驱动_1_seg_3 ), .Seg_4(\数码管驱动_1_seg_4 ),
    .Seg_5(\数码管驱动_1_seg_5 ), .Seg_6(\数码管驱动_1_seg_6 ), .Seg_7(\数码管驱动_1_seg_7 ));
  _7_Segment_Display u_7_segment_display_1 (
    .g(\数码管驱动_1_seg_1 ), .f(\数码管驱动_1_seg_2 ), .a(\数码管驱动_1_seg_3 ), .b(\数码管驱动_1_seg_4 ), .e(\数码管驱动_1_seg_5 ),
    .d(\数码管驱动_1_seg_6 ), .c(\数码管驱动_1_seg_7 ));  // open: dp

  // Notes on the sheet:
  //   Ctrl+T驱动时钟单步运行测试
endmodule

// 4位数比较器
module \_4位无符号比较器  (
  input  X3,
  input  X2,
  input  X1,
  input  X0,
  input  Y3,
  input  Y2,
  input  Y1,
  input  Y0,
  output Great,
  output Equal,
  output Less
);

  wire and_1_out, and_2_out, and_3_out, and_4_out, and_5_out, and_6_out, and_7_out, and_8_out, and_9_out,
       and_10_out, and_11_out, and_12_out, and_13_out, and_14_out, and_15_out, and_16_out, and_17_out,
       and_18_out, and_19_out, and_20_out, and_21_out, and_22_out, and_23_out, and_24_out, and_25_out,
       and_26_out, and_27_out, and_28_out, and_29_out, and_30_out, and_31_out, and_32_out, and_33_out,
       and_34_out, and_35_out, and_37_out, and_38_out, and_39_out, and_40_out, not_1_out, not_2_out,
       not_3_out, not_4_out, not_5_out, not_6_out, not_7_out, not_8_out, not_9_out, not_10_out, not_11_out,
       not_12_out, not_13_out, not_14_out, not_15_out, not_16_out, not_17_out, not_18_out, not_19_out,
       not_20_out, not_21_out, not_22_out, not_23_out, not_24_out, not_25_out, not_26_out, not_27_out,
       not_28_out, not_29_out, not_30_out, not_31_out, not_32_out, not_33_out, not_34_out, not_35_out,
       not_36_out, not_37_out, not_38_out, not_39_out, not_40_out, not_41_out, not_42_out, not_43_out,
       not_44_out, not_45_out, not_46_out, not_47_out, not_48_out, not_49_out, not_50_out, not_51_out,
       not_52_out, not_53_out, not_54_out, not_55_out, not_56_out, or_1_out, or_2_out, or_3_out, or_4_out,
       or_5_out, or_6_out, or_7_out, or_8_out, or_9_out, or_10_out;

  not not_1 (not_1_out, Y3);
  not not_2 (not_2_out, Y2);
  not not_3 (not_3_out, Y1);
  not not_4 (not_4_out, Y0);
  not not_5 (not_5_out, Y3);
  not not_6 (not_6_out, Y2);
  not not_7 (not_7_out, Y1);
  not not_8 (not_8_out, Y3);
  not not_9 (not_9_out, Y2);
  not not_10 (not_10_out, Y0);
  not not_11 (not_11_out, Y3);
  not not_12 (not_12_out, Y2);
  not not_13 (not_13_out, Y3);
  not not_14 (not_14_out, Y1);
  not not_15 (not_15_out, Y0);
  not not_16 (not_16_out, Y3);
  not not_17 (not_17_out, Y1);
  not not_18 (not_18_out, Y3);
  not not_19 (not_19_out, Y0);
  not not_20 (not_20_out, Y3);
  not not_21 (not_21_out, Y2);
  not not_22 (not_22_out, Y1);
  not not_23 (not_23_out, Y0);
  not not_24 (not_24_out, Y2);
  not not_25 (not_25_out, Y1);
  not not_26 (not_26_out, Y2);
  not not_27 (not_27_out, Y0);
  not not_28 (not_28_out, Y2);
  not not_29 (not_29_out, Y1);
  not not_30 (not_30_out, Y0);
  not not_31 (not_31_out, Y1);
  not not_32 (not_32_out, Y0);
  and and_1 (and_1_out, X3, Y3);
  not not_33 (not_33_out, X3);
  and and_2 (and_2_out, not_33_out, not_34_out);
  not not_34 (not_34_out, Y3);
  and and_3 (and_3_out, X2, Y2);
  not not_35 (not_35_out, X2);
  and and_4 (and_4_out, not_35_out, not_36_out);
  not not_36 (not_36_out, Y2);
  and and_5 (and_5_out, X1, Y1);
  not not_37 (not_37_out, X1);
  and and_6 (and_6_out, not_37_out, not_38_out);
  not not_38 (not_38_out, Y1);
  and and_7 (and_7_out, X0, Y0);
  not not_39 (not_39_out, X0);
  and and_8 (and_8_out, not_39_out, not_40_out);
  not not_40 (not_40_out, Y0);
  not not_41 (not_41_out, X3);
  not not_42 (not_42_out, Y3);
  and and_9 (and_9_out, X3, Y3);
  not not_43 (not_43_out, X3);
  and and_10 (and_10_out, not_43_out, not_44_out);
  not not_44 (not_44_out, Y3);
  and and_11 (and_11_out, X2, Y2);
  not not_45 (not_45_out, X2);
  and and_12 (and_12_out, not_45_out, not_46_out);
  not not_46 (not_46_out, Y2);
  and and_13 (and_13_out, X3, Y3);
  not not_47 (not_47_out, X3);
  and and_14 (and_14_out, not_47_out, not_48_out);
  not not_48 (not_48_out, Y3);
  and and_15 (and_15_out, X2, Y2);
  not not_49 (not_49_out, X2);
  and and_16 (and_16_out, not_49_out, not_50_out);
  not not_50 (not_50_out, Y2);
  and and_17 (and_17_out, X1, Y1);
  not not_51 (not_51_out, X1);
  and and_18 (and_18_out, not_51_out, not_52_out);
  not not_52 (not_52_out, Y1);
  and and_19 (and_19_out, X0, not_1_out, not_2_out, not_3_out, not_4_out);
  and and_20 (and_20_out, X1, not_5_out, not_6_out, not_7_out);
  and and_21 (and_21_out, X1, X0, not_8_out, not_9_out, not_10_out);
  and and_22 (and_22_out, X2, not_11_out, not_12_out);
  and and_23 (and_23_out, X2, X0, not_13_out, not_14_out, not_15_out);
  and and_24 (and_24_out, X2, X1, not_16_out, not_17_out);
  and and_25 (and_25_out, X2, X1, X0, not_18_out, not_19_out);
  and and_26 (and_26_out, X3, not_20_out);
  and and_27 (and_27_out, X3, X0, not_21_out, not_22_out, not_23_out);
  and and_28 (and_28_out, X3, X1, not_24_out, not_25_out);
  and and_29 (and_29_out, X3, X1, X0, not_26_out, not_27_out);
  and and_30 (and_30_out, X3, X2, not_28_out);
  and and_31 (and_31_out, X3, X2, X0, not_29_out, not_30_out);
  and and_32 (and_32_out, X3, X2, X1, not_31_out);
  and and_33 (and_33_out, X3, X2, X1, X0, not_32_out);
  or or_1 (or_1_out, and_1_out, and_2_out);
  or or_2 (or_2_out, and_3_out, and_4_out);
  or or_3 (or_3_out, and_5_out, and_6_out);
  or or_4 (or_4_out, and_7_out, and_8_out);
  not not_53 (not_53_out, X3);
  and and_34 (and_34_out, X3, Y3);
  or or_5 (or_5_out, and_34_out, and_35_out);
  and and_35 (and_35_out, not_41_out, not_42_out);
  not not_54 (not_54_out, X2);
  or or_6 (or_6_out, and_9_out, and_10_out);
  or or_7 (or_7_out, and_11_out, and_12_out);
  not not_55 (not_55_out, X1);
  or or_8 (or_8_out, and_13_out, and_14_out);
  or or_9 (or_9_out, and_15_out, and_16_out);
  or or_10 (or_10_out, and_17_out, and_18_out);
  not not_56 (not_56_out, X0);
  or or_11 (Great, and_19_out, and_20_out, and_21_out, and_22_out, and_23_out, and_24_out, and_25_out, and_26_out, and_27_out, and_28_out, and_29_out, and_30_out, and_31_out, and_32_out, and_33_out);
  and and_36 (Equal, or_1_out, or_2_out, or_3_out, or_4_out);
  and and_37 (and_37_out, Y3, not_53_out);
  and and_38 (and_38_out, or_5_out, Y2, not_54_out);
  and and_39 (and_39_out, or_6_out, or_7_out, Y1, not_55_out);
  and and_40 (and_40_out, or_8_out, or_9_out, or_10_out, Y0, not_56_out);
  or or_12 (Less, and_37_out, and_38_out, and_39_out, and_40_out);
endmodule

module \_8位无符号比较器  (
  input  [7:0] X,
  input  [7:0] Y,
  output Great,
  output Equal,
  output Less
);

  // Probe on X
  // Probe on Y
  \_4位无符号比较器  \u_4位无符号比较器_1  ();  // open: X3, X2, X1, X0, Y3, Y2, Y1, Y0, Great, Equal, Less
  \_4位无符号比较器  \u_4位无符号比较器_2  ();  // open: X3, X2, X1, X0, Y3, Y2, Y1, Y0, Great, Equal, Less

  // Other names for the same wires on the sheet: X0[3:0] = X[3:0]; X1[3:0] = X[7:4]; Y0[3:0] = Y[3:0];
  //   Y1[3:0] = Y[7:4]

  // Notes on the sheet:
  //   电路功能：X,Y进行无符号比较，Great=(X>Y)?1:0;
  //   输入引脚区
  //   输出引脚区
endmodule

// MUX
module \_2路选择器_1位  (
  input  X0,
  input  Sel,
  input  X1,
  output Out
);


  // Notes on the sheet:
  //   输入引脚区
  //   电路功能：Out=(Sel==0)?X0:X1;
  //   请勿增删改引脚，请在下方利用上方输入输出引脚的隧道标签信号构建电路，ctrl+d复制选择组件
  //   输出引脚区
endmodule

// MUX
module \_2路选择器_8位  (
  input  [7:0] X,
  input  Sel,
  input  [7:0] Y,
  output [7:0] Out
);

  // Probe on X
  // Probe on Y
  // Probe on Out

  // Notes on the sheet:
  //   输入引脚区
  //   电路功能：Out=(Sel==0)?X:Y;
  //   请勿增删改引脚，请在下方利用上方输入输出引脚的隧道标签信号构建电路，ctrl+d复制选择组件
  //   输出引脚区
endmodule

// 计数器
module \BCD双向计数器_可异步置位  (
  input  CLK,
  input  \使能 ,
  input  \异步置位控制 ,
  input  [3:0] \异步预置 ,
  input  \Mode_0正计数_1倒计数 ,
  output [3:0] \输出Q ,
  output \进位_借位 
);

  wire D0, D1, D2, D3, undriven;

  \BCD双向计数器状态转换_自动生成  \bcd双向计数器状态转换_自动生成_1  ();  // open: S3, N3, S2, N2, S1, N1, S0, N0, Mode
  \BCD双向计数器输出函数_自动生成  \bcd双向计数器输出函数_自动生成_1  (.Cout(\进位_借位 ));  // open: S3, S2, S1, S0, Mode
  assign {D3, D2, D1, D0} = \异步置位控制  ? \异步预置  : 4'bz;  // Controlled_Buffer controlled_buffer_1
  D_Flip_Flop u_D3 ();  // open: clk, D, Q, Qn, preset, en, reset
  D_Flip_Flop u_D2 ();  // open: clk, D, Q, Qn, preset, en, reset
  D_Flip_Flop u_D1 (.reset(undriven));  // open: clk, D, Q, Qn, preset, en
  D_Flip_Flop u_D0 ();  // open: clk, D, Q, Qn, preset, en, reset
  // Probe on \输出Q 

  // Other names for the same wires on the sheet: Cout = \进位_借位 ; Din[3:0] = \异步预置 ; En = \使能 ;
  //   Mode = \Mode_0正计数_1倒计数 ; PreSet = \异步置位控制 ; Q[3:0] = \输出Q 

  // Notes on the sheet:
  //   正计数到9，倒计数到0时输出为1
endmodule

// 状态转换
module \BCD双向计数器状态转换_自动生成  (
  input  S3,
  input  S2,
  input  S1,
  input  S0,
  input  Mode,
  output N3,
  output N2,
  output N1,
  output N0
);
endmodule

module \BCD双向计数器输出函数_自动生成  (
  input  S3,
  input  S2,
  input  S1,
  input  S0,
  input  Mode,
  output Cout
);
endmodule

// 倒计数
module \双位十进制双向计数器  (
  input  CLK,
  input  \使能 ,
  input  \异步置位控制 ,
  input  [7:0] \异步预置 ,
  input  \Mode_0正计数_1倒计数 ,
  output [7:0] Q,
  output \进位_借位 
);

  \BCD双向计数器_可异步置位  \bcd双向计数器_可异步置位_1  ();  // open: CLK, 使能, 异步置位控制, 异步预置, Mode_0正计数_1倒计数, 输出Q, 进位_借位
  \BCD双向计数器_可异步置位  \bcd双向计数器_可异步置位_2  ();  // open: CLK, 使能, 异步置位控制, 异步预置, Mode_0正计数_1倒计数, 输出Q, 进位_借位
  // Probe on Q

  // Other names for the same wires on the sheet: Cout = \进位_借位 ; Din[7:0] = \异步预置 ; Din0[3:0] = \异步预置 [3:0];
  //   Din1[3:0] = \异步预置 [7:4]; En = \使能 ; Mode = \Mode_0正计数_1倒计数 ; PreSet = \异步置位控制 

  // Notes on the sheet:
  //   正计数到9，倒计数到0时输出为1
endmodule

// 状态机
module \红绿灯状态机_自动生成  (
  input  S2,
  input  S1,
  input  S0,
  input  T1,
  input  T2,
  input  T3,
  input  T4,
  input  EMERG,
  output N2,
  output N1,
  output N0
);
endmodule

// 输出函数
module \红绿灯状态输出函数_真值表  (
  input  S2,
  input  S1,
  input  S0,
  output R1,
  output Y1,
  output G1,
  output R2,
  output Y2,
  output G2,
  output PASS1,
  output PASS2
);
endmodule

module \红绿灯  (
  input  in_1,
  output R1,
  output Y1,
  output [2:0] Status,
  output G1,
  output R2,
  output Y2,
  output [7:0] Timer,
  output G2
);

  wire CLK, RST, T1, T2, undriven, undriven_3, Y1c, Y2c, \紧急情况 ;
  wire [2:0] S1B, S2B;
  wire [3:0] S1T, S2T;
  wire [7:0] counter_1_q, Timer1, undriven_2;

  LED led_1 (.in(R1));
  LED led_2 (.in(Y1c));
  LED led_3 (.in(G1));
  _7_Segment_Display u_7_segment_display_1 (
    .g(S2T[0]), .f(S2T[1]), .a(S2T[2]), .b(S2T[3]), .e(S2B[0]), .d(S2B[1]), .c(S2B[2]));  // open: dp
  _7_Segment_Display u_7_segment_display_2 (
    .g(S1T[0]), .f(S1T[1]), .a(S1T[2]), .b(S1T[3]), .e(S1B[0]), .d(S1B[1]), .c(S1B[2]));  // open: dp
  Register #(.width(3)) \u_状态  (.Q(Status), .clk(CLK));  // open: D, en, clr
  \双位十进制双向计数器  \u_双位十进制双向计数器_1  (.CLK(CLK), .\异步预置 (8'h20));  // open: 使能, 异步置位控制, Mode_0正计数_1倒计数, Q, 进位_借位
  \红绿灯状态输出函数_真值表  \u_红绿灯状态输出函数_真值表_1  ();  // open: S2, R1, S1, Y1, S0, G1, R2, Y2, G2, PASS1, PASS2
  LED led_4 (.in(R2));
  LED led_5 (.in(Y2c));
  LED led_6 (.in(G2));
  or or_1 (\紧急情况 , in_1, undriven);
  \红绿灯状态机_自动生成  \u_红绿灯状态机_自动生成_1  ();  // open: S2, N2, S1, N1, S0, N0, T1, T2, T3, T4, EMERG
  \_8位无符号比较器  \u_8位无符号比较器_1  (.X(Timer1), .Y(8'h4), .Equal(T1));  // open: Great, Less
  \_8位无符号比较器  \u_8位无符号比较器_2  (.Y(8'h1), .Equal(T2));  // open: X, Great, Less
  and and_1 (Y1c, Y1, CLK);
  and and_2 (Y2c, Y2, CLK);
  Clock clock_1 (.out(CLK));
  \_2路选择器_8位  \u_2路选择器_8位_1  (.X(Timer1), .Sel(undriven_3), .Y(undriven_2), .Out(Timer));
  D_Flip_Flop d_ff_1 (.clk(CLK), .D(1'b1), .Qn(RST));  // open: Q, preset, en, reset
  Counter counter_1 (.Q(counter_1_q), .clk(CLK));  // open: load, D, count, carry, clr
  // Probe on counter_1_q
  \数码管驱动  \u_数码管驱动_1  ();  // open: X3, X2, X1, Seg_1, X0, Seg_2, Seg_3, Seg_4, Seg_5, Seg_6, Seg_7
  \数码管驱动  \u_数码管驱动_2  ();  // open: X3, X2, X1, Seg_1, X0, Seg_2, Seg_3, Seg_4, Seg_5, Seg_6, Seg_7

  // Other names for the same wires on the sheet: E = in_1

  // Notes on the sheet:
  //   主道红绿灯
  //   测试时要求主道20秒，辅道10秒
  //   倒计时
  //   状态机现态
  //   主道计时逻辑
  //   辅道红绿灯
  //   状态机现态
  //   当前倒计时
  //   引脚区，用于EduCoder测试
  //   控制黄灯闪烁
  //   初始化信号，第一拍为1
  //   用于预置计数器初始值
  //   当前倒计时
  //   时钟计数
endmodule
